// Logisim project AmongUs.circ as structural Verilog: 1 circuit, main circuit main
module main (
);

  wire and_1_out, and_2_out, button_1_out, clock_1_out, clock_2_out, tunnel, tunnel_t;
  wire [1:0] counter_1_q;
  wire [3:0] counter_2_q;
  wire [24:0] _0, _1, _2, _3, _4, _5, _6, _7, _8, _9, _10, _11, _12, _13, _14, _15, _16, _17, _18, _19, _20,
       _21, p1, p2, p3, p4, p5, p6, p7, p8, p9, p10, pp1, pp2, pp3, pp4, ppp1, ppp2, ppp3, ppp4;

  Clock clock_1 (.out(clock_1_out));
  Counter #(.width(2), .max('h2), .ongoal("stay")) counter_1 (
    .Q(counter_1_q), .clk(and_1_out), .clr(tunnel));  // open: load, D, count, carry
  and and_1 (and_1_out, clock_1_out, tunnel_t);
  Button button_1 (.out(button_1_out));
  T_Flip_Flop t_ff_1 (.clk(button_1_out), .T(1'b1), .Q(tunnel_t), .Qn(tunnel));  // open: preset, reset, en
  Multiplexer #(.select(2), .width(25)) multiplexer_1 (
    .in0({25{1'b0}}), .in2({25{1'b0}}), .out(_0), .sel(counter_1_q));  // open: in1, in3, en
  Multiplexer #(.select(2), .width(25)) multiplexer_2 (
    .in0({25{1'b0}}), .in2({25{1'b0}}), .out(_1), .sel(counter_1_q));  // open: in1, in3, en
  Multiplexer #(.select(2), .width(25)) multiplexer_3 (
    .in2({25{1'b0}}), .out(_2), .sel(counter_1_q));  // open: in0, in1, in3, en
  Multiplexer #(.select(2), .width(25)) multiplexer_4 (
    .in0({p1[24:15], {8{1'b0}}, p1[6:0]}), .in1({pp1[24:10], 3'b000, pp1[6:0]}), .in2({25{1'b0}}), .out(_3),
    .sel(counter_1_q));  // open: in3, en
  Multiplexer #(.select(2), .width(25)) multiplexer_5 (
    .in0({p1[24:15], {8{1'b0}}, p1[6:0]}), .in1({pp1[24:10], 3'b000, pp1[6:0]}), .out(_4), .sel(counter_1_q));  // open: in2, in3, en
  DotMatrix #(.matrixcols(22), .matrixrows(25)) dotmatrix_1 (
    .col0(_0), .col1(_1), .col2(_2), .col3(_3), .col4(_4), .col5(_5), .col6(_6), .col7(_7), .col8(_8),
    .col9(_9), .col10(_10), .col11(_11), .col12(_12), .col13(_13), .col14(_14), .col15(_15), .col16(_16),
    .col17(_17), .col18(_18), .col19(_19), .col20(_20), .col21(_21));
  Multiplexer #(.select(2), .width(25)) multiplexer_6 (
    .in2({ppp1[24:13], 3'b000, ppp1[9:6], 3'b000, ppp1[2:0]}), .out(_5), .sel(counter_1_q));  // open: in0, in1, in3, en
  Multiplexer #(.select(2), .width(25)) multiplexer_7 (
    .in0({p2[24:18], {15{1'b0}}, p2[2:0]}), .in1({pp2[24:10], {8{1'b0}}, pp2[1:0]}),
    .in2({ppp1[24:13], 3'b000, ppp1[9:6], 3'b000, ppp1[2:0]}), .out(_6), .sel(counter_1_q));  // open: in3, en
  Multiplexer #(.select(2), .width(25)) multiplexer_8 (
    .in0({p3[24:19], {16{1'b0}}, p3[2:0]}), .in1({pp2[24:10], {8{1'b0}}, pp2[1:0]}),
    .in2({ppp1[24:13], 3'b000, ppp1[9:6], 3'b000, ppp1[2:0]}), .out(_7), .sel(counter_1_q));  // open: in3, en
  Multiplexer #(.select(2), .width(25)) multiplexer_9 (
    .in0({p4[24:20], 4'b0000, p4[15:13], {10{1'b0}}, p4[2:0]}), .in1({pp2[24:10], {8{1'b0}}, pp2[1:0]}),
    .in2({ppp2[24:13], {10{1'b0}}, ppp2[2:0]}), .out(_8), .sel(counter_1_q));  // open: in3, en
  Multiplexer #(.select(2), .width(25)) multiplexer_10 (
    .in0({p5[24:20], 3'b000, p5[16:12], {6{1'b0}}, p5[5:0]}), .in1({pp3[24:10], 4'b0000, pp3[5:0]}),
    .in2({ppp3[24:16], 2'b00, ppp3[13], {10{1'b0}}, ppp3[2:0]}), .out(_9), .sel(counter_1_q));  // open: in3, en
  Multiplexer #(.select(2), .width(25)) multiplexer_11 (
    .in0({p6[24:20], 2'b00, p6[17:11], {5{1'b0}}, p6[5:0]}), .in1({pp4[24:9], 3'b000, pp4[5:0]}),
    .in2({ppp3[24:16], 2'b00, ppp3[13], {10{1'b0}}, ppp3[2:0]}), .out(_10), .sel(counter_1_q));  // open: in3, en
  Multiplexer #(.select(2), .width(25)) multiplexer_12 (
    .in0({p7[24:20], 2'b00, p7[17:11], {5{1'b0}}, p7[5:0]}), .in1({pp4[24:9], 3'b000, pp4[5:0]}),
    .in2({ppp4[24:16], 2'b00, ppp4[13], 4'b0000, ppp4[8:6], 3'b000, ppp4[2:0]}), .out(_11), .sel(counter_1_q));  // open: in3, en
  Multiplexer #(.select(2), .width(25)) multiplexer_13 (
    .in0({p7[24:20], 2'b00, p7[17:11], {5{1'b0}}, p7[5:0]}), .in1({pp4[24:9], 3'b000, pp4[5:0]}), .out(_12),
    .sel(counter_1_q));  // open: in2, in3, en
  Multiplexer #(.select(2), .width(25)) multiplexer_14 (
    .in0({p8[24:20], 2'b00, p8[17:11], {8{1'b0}}, p8[2:0]}), .in1({pp4[24:9], 3'b000, pp4[5:0]}), .out(_13),
    .sel(counter_1_q));  // open: in2, in3, en
  Multiplexer #(.select(2), .width(25)) multiplexer_15 (
    .in0({p9[24:19], 1'b0, p9[17:11], {8{1'b0}}, p9[2:0]}), .in1({pp2[24:10], {8{1'b0}}, pp2[1:0]}),
    .out(_14), .sel(counter_1_q));  // open: in2, in3, en
  Multiplexer #(.select(2), .width(25)) multiplexer_16 (
    .in0({p10[24:11], {8{1'b0}}, p10[2:0]}), .in1({pp2[24:10], {8{1'b0}}, pp2[1:0]}), .out(_15),
    .sel(counter_1_q));  // open: in2, in3, en
  Multiplexer #(.select(2), .width(25)) multiplexer_17 (
    .in1({pp2[24:10], {8{1'b0}}, pp2[1:0]}), .out(_16), .sel(counter_1_q));  // open: in0, in2, in3, en
  Multiplexer #(.select(2), .width(25)) multiplexer_18 (.out(_17), .sel(counter_1_q));  // open: in0, in1, in2, in3, en
  Multiplexer #(.select(2), .width(25)) multiplexer_19 (
    .in0({25{1'b0}}), .out(_18), .sel(counter_1_q));  // open: in1, in2, in3, en
  Multiplexer #(.select(2), .width(25)) multiplexer_20 (
    .in0({25{1'b0}}), .out(_19), .sel(counter_1_q));  // open: in1, in2, in3, en
  Counter #(.width(4), .max('h2), .ongoal("stay")) counter_2 (
    .Q(counter_2_q), .clk(and_2_out), .clr(tunnel));  // open: load, D, count, carry
  and and_2 (and_2_out, clock_2_out, tunnel_t);
  Clock clock_2 (.out(clock_2_out));
  Multiplexer #(.select(2), .width(25)) multiplexer_21 (
    .in0({25{1'b0}}), .out(_20), .sel(counter_1_q));  // open: in1, in2, in3, en
  Multiplexer #(.select(2), .width(25)) multiplexer_22 (
    .in0({25{1'b0}}), .out(_21), .sel(counter_1_q));  // open: in1, in2, in3, en
  ROM #(.addrWidth(4), .dataWidth(25)) rom_1 (.addr(counter_2_q), .data(_0));  // open: sel
  ROM #(.addrWidth(4), .dataWidth(25)) rom_2 (.addr(counter_2_q), .data(_1));  // open: sel
  ROM #(.addrWidth(4), .dataWidth(25)) rom_3 (.addr(counter_2_q), .data(_2));  // open: sel
  ROM #(.addrWidth(4), .dataWidth(25)) rom_4 (.addr(counter_2_q), .data(_3));  // open: sel
  ROM #(.addrWidth(4), .dataWidth(25)) rom_5 (.addr(counter_2_q), .data(_4));  // open: sel
  ROM #(.addrWidth(4), .dataWidth(25)) rom_6 (.addr(counter_2_q), .data(_5));  // open: sel
  ROM #(.addrWidth(4), .dataWidth(25)) rom_7 (.addr(counter_2_q), .data(_6));  // open: sel
  ROM #(.addrWidth(4), .dataWidth(25)) rom_8 (.addr(counter_2_q), .data(_7));  // open: sel
  ROM #(.addrWidth(4), .dataWidth(25)) rom_9 (.addr(counter_2_q), .data(_8));  // open: sel
  ROM #(.addrWidth(4), .dataWidth(25)) rom_10 (.addr(counter_2_q), .data(_9));  // open: sel
  ROM #(.addrWidth(4), .dataWidth(25)) rom_11 (.addr(counter_2_q), .data(_10));  // open: sel
  ROM #(.addrWidth(4), .dataWidth(25)) rom_12 (.addr(counter_2_q), .data(_11));  // open: sel
  ROM #(.addrWidth(4), .dataWidth(25)) rom_13 (.addr(counter_2_q), .data(_12));  // open: sel
  ROM #(.addrWidth(4), .dataWidth(25)) rom_14 (.addr(counter_2_q), .data(_13));  // open: sel
  ROM #(.addrWidth(4), .dataWidth(25)) rom_15 (.addr(counter_2_q), .data(_14));  // open: sel
  ROM #(.addrWidth(4), .dataWidth(25)) rom_16 (.addr(counter_2_q), .data(_15));  // open: sel
  ROM #(.addrWidth(4), .dataWidth(25)) rom_17 (.addr(counter_2_q), .data(_16));  // open: sel
  ROM #(.addrWidth(4), .dataWidth(25)) rom_18 (.addr(counter_2_q), .data(_17));  // open: sel
  ROM #(.addrWidth(4), .dataWidth(25)) rom_19 (.addr(counter_2_q), .data(_18));  // open: sel
  ROM #(.addrWidth(4), .dataWidth(25)) rom_20 (.addr(counter_2_q), .data(_19));  // open: sel
  ROM #(.addrWidth(4), .dataWidth(25)) rom_21 (.addr(counter_2_q), .data(_20));  // open: sel
  ROM #(.addrWidth(4), .dataWidth(25)) rom_22 (.addr(counter_2_q), .data(_21));  // open: sel

  // Other names for the same wires on the sheet: a[24:0] = _0; b[24:0] = _1; c[24:0] = _2; d[24:0] = _3; e[24:0] = _4;
  //   f[24:0] = _5; g[24:0] = _6; h[24:0] = _7; i[24:0] = _8; j[24:0] = _9; k[24:0] = _10; l[24:0] = _11;
  //   m[24:0] = _12; n[24:0] = _13; o[24:0] = _14; p[24:0] = _15; q[24:0] = _16; r[24:0] = _17; s[24:0] = _18;
  //   t[24:0] = _19; u[24:0] = _20; v[24:0] = _21

  // Notes on the sheet:
  //   contents of rom_3 (hex, n*v repeats v):
  //   7f80 780
  //   contents of rom_4 (hex, n*v repeats v):
  //   ffc0 7c0
  //   contents of rom_5 (hex, n*v repeats v):
  //   ffc0 7c0 1c38
  //   contents of rom_6 (hex, n*v repeats v):
  //   3fff8 7fc 3e7c
  //   contents of rom_7 (hex, n*v repeats v):
  //   7fffc 7fe 3e7c
  //   contents of rom_8 (hex, n*v repeats v):
  //   ffffc 7fe 3ffc
  //   contents of rom_9 (hex, n*v repeats v):
  //   1ffffc 7fe fffc
  //   contents of rom_10 (hex, n*v repeats v):
  //   1f1ff8 37fc 1fffc
  //   contents of rom_11 (hex, n*v repeats v):
  //   1e0fe0 4fe0 1fffc
  //   contents of rom_12 (hex, n*v repeats v):
  //   1e0fe0 23e0 1fffc
  //   contents of rom_13 (hex, n*v repeats v):
  //   1e0ff8 4fe0 1ff7c
  //   contents of rom_14 (hex, n*v repeats v):
  //   1e0ffc 37fc 140
  //   contents of rom_15 (hex, n*v repeats v):
  //   e0ffc 7fe 220
  //   contents of rom_16 (hex, n*v repeats v):
  //   60ffc 7fe 2a0
  //   contents of rom_17 (hex, n*v repeats v):
  //   11ff8 7fe 140
  //   contents of rom_18 (hex, n*v repeats v):
  //   e000 7fc
endmodule
