// Logisim project Contador Hexadecimal.circ as structural Verilog: 1 circuit, main circuit main
module main (
);

  wire clock_1_out;
  wire [3:0] t_ff_1_q;
  wire [19:0] rom_1_data;

  Clock clock_1 (.out(clock_1_out));
  T_Flip_Flop #(.trigger("falling")) t_ff_1 (
    .clk(clock_1_out), .T(1'b1), .Q(t_ff_1_q[0]));  // open: Qn, preset, reset, en
  T_Flip_Flop #(.trigger("falling")) t_ff_2 (
    .clk(t_ff_1_q[0]), .T(1'b1), .Q(t_ff_1_q[1]));  // open: Qn, preset, reset, en
  T_Flip_Flop #(.trigger("falling")) t_ff_3 (
    .clk(t_ff_1_q[1]), .T(1'b1), .Q(t_ff_1_q[2]));  // open: Qn, preset, reset, en
  T_Flip_Flop #(.trigger("falling")) t_ff_4 (
    .clk(t_ff_1_q[2]), .T(1'b1), .Q(t_ff_1_q[3]));  // open: Qn, preset, reset, en
  ROM #(.addrWidth(4), .dataWidth(20)) rom_1 (.addr(t_ff_1_q), .data(rom_1_data));  // open: sel
  DotMatrix #(.matrixcols(4), .matrixrows(5)) dotmatrix_1 (
    .col0(rom_1_data[19:15]), .col1(rom_1_data[14:10]), .col2(rom_1_data[9:5]), .col3(rom_1_data[4:0]));

  // Notes on the sheet:
  //   contents of rom_1 (hex, n*v repeats v):
  //   fc63f 11f bd6bd 46bb e109f ed6b7 fd6b7 421f dd6bb e529f fd29f fd6bb fc631 fc62e fd6b1 fd290
endmodule
