// Logisim project Eclipse.circ as structural Verilog: 1 circuit, main circuit main
module main (
);

  wire clock_1_out;
  wire [7:0] counter_1_q;
  wire [30:0] a, aa, b, bb, c, cc, d, dd, e, ee, f, g, h, i, j, k, l, m, n, o, p, q, r, s, t, u, v, w, x, y,
       z;

  Clock clock_1 (.out(clock_1_out));
  Counter #(.max('h18), .ongoal("stay")) counter_1 (
    .Q(counter_1_q), .clk(clock_1_out));  // open: load, D, count, carry, clr
  ROM #(.dataWidth(31)) rom_1 (.addr(counter_1_q), .data(a));  // open: sel
  ROM #(.dataWidth(31)) rom_2 (.addr(counter_1_q), .data(b));  // open: sel
  ROM #(.dataWidth(31)) rom_3 (.addr(counter_1_q), .data(c));  // open: sel
  ROM #(.dataWidth(31)) rom_4 (.addr(counter_1_q), .data(d));  // open: sel
  ROM #(.dataWidth(31)) rom_5 (.addr(counter_1_q), .data(e));  // open: sel
  ROM #(.dataWidth(31)) rom_6 (.addr(counter_1_q), .data(f));  // open: sel
  ROM #(.dataWidth(31)) rom_7 (.addr(counter_1_q), .data(g));  // open: sel
  ROM #(.dataWidth(31)) rom_8 (.addr(counter_1_q), .data(h));  // open: sel
  ROM #(.dataWidth(31)) rom_9 (.addr(counter_1_q), .data(i));  // open: sel
  ROM #(.dataWidth(31)) rom_10 (.addr(counter_1_q), .data(j));  // open: sel
  DotMatrix #(.matrixcols(31), .matrixrows(31)) dotmatrix_1 (
    .col0(a), .col1(b), .col2(c), .col3(d), .col4(e), .col5(f), .col6(g), .col7(h), .col8(i), .col9(j),
    .col10(k), .col11(l), .col12(m), .col13(n), .col14(o), .col15(p), .col16(q), .col17(r), .col18(s),
    .col19(t), .col20(u), .col21(v), .col22(w), .col23(x), .col24(y), .col25(z), .col26(aa), .col27(bb),
    .col28(cc), .col29(dd), .col30(ee));
  ROM #(.dataWidth(31)) rom_11 (.addr(counter_1_q), .data(k));  // open: sel
  ROM #(.dataWidth(31)) rom_12 (.addr(counter_1_q), .data(l));  // open: sel
  ROM #(.dataWidth(31)) rom_13 (.addr(counter_1_q), .data(m));  // open: sel
  ROM #(.dataWidth(31)) rom_14 (.addr(counter_1_q), .data(n));  // open: sel
  ROM #(.dataWidth(31)) rom_15 (.addr(counter_1_q), .data(o));  // open: sel
  ROM #(.dataWidth(31)) rom_16 (.addr(counter_1_q), .data(p));  // open: sel
  ROM #(.dataWidth(31)) rom_17 (.addr(counter_1_q), .data(q));  // open: sel
  ROM #(.dataWidth(31)) rom_18 (.addr(counter_1_q), .data(r));  // open: sel
  ROM #(.dataWidth(31)) rom_19 (.addr(counter_1_q), .data(s));  // open: sel
  ROM #(.dataWidth(31)) rom_20 (.addr(counter_1_q), .data(t));  // open: sel
  ROM #(.dataWidth(31)) rom_21 (.addr(counter_1_q), .data(u));  // open: sel
  ROM #(.dataWidth(31)) rom_22 (.addr(counter_1_q), .data(v));  // open: sel
  ROM #(.dataWidth(31)) rom_23 (.addr(counter_1_q), .data(w));  // open: sel
  ROM #(.dataWidth(31)) rom_24 (.addr(counter_1_q), .data(x));  // open: sel
  ROM #(.dataWidth(31)) rom_25 (.addr(counter_1_q), .data(y));  // open: sel
  ROM #(.dataWidth(31)) rom_26 (.addr(counter_1_q), .data(z));  // open: sel
  ROM #(.dataWidth(31)) rom_27 (.addr(counter_1_q), .data(aa));  // open: sel
  ROM #(.dataWidth(31)) rom_28 (.addr(counter_1_q), .data(bb));  // open: sel
  ROM #(.dataWidth(31)) rom_29 (.addr(counter_1_q), .data(cc));  // open: sel
  ROM #(.dataWidth(31)) rom_30 (.addr(counter_1_q), .data(dd));  // open: sel
  ROM #(.dataWidth(31)) rom_31 (.addr(counter_1_q), .data(ee));  // open: sel

  // Notes on the sheet:
  //   contents of rom_8 (hex, n*v repeats v):
  //   24*0 3e000
  //   contents of rom_9 (hex, n*v repeats v):
  //   24*0 c1800
  //   contents of rom_10 (hex, n*v repeats v):
  //   24*0 100400
  //   contents of rom_11 (hex, n*v repeats v):
  //   24*0 200200
  //   contents of rom_12 (hex, n*v repeats v):
  //   24*0 400100 10000000
  //   contents of rom_13 (hex, n*v repeats v):
  //   24*0 400100
  //   contents of rom_14 (hex, n*v repeats v):
  //   24*0 800080
  //   contents of rom_15 (hex, n*v repeats v):
  //   23*0 800080 800080
  //   contents of rom_16 (hex, n*v repeats v):
  //   22*0 800080 800080 800080
  //   contents of rom_17 (hex, n*v repeats v):
  //   15*0 3e000 ff800 1c1c00 100400 200200 400100 4*800080
  //   contents of rom_18 (hex, n*v repeats v):
  //   14*0 3e000 ff800 1ffc00 3ffe00 3c1e00 700700 e00380 c00180 800080 800080 800080
  //   contents of rom_19 (hex, n*v repeats v):
  //   13*0 3e000 ff800 1ffc00 3ffe00 7fff00 7fff00 fc1f80 f00780 e00380 c00180 800080 400100
  //   contents of rom_20 (hex, n*v repeats v):
  //   12*0 3e000 ff800 1ffc00 3ffe00 7fff00 7fff00 ffff80 ffff80 fc1f80 f00780 e00380 400100 400100
  //   contents of rom_21 (hex, n*v repeats v):
  //   11*0 3e000 ff800 1ffc00 3ffe00 7fff00 7fff00 4*ffff80 fc1f80 700700 600300 200200
  //   contents of rom_22 (hex, n*v repeats v):
  //   10*0 3e000 ff800 1ffc00 3ffe00 7fff00 7fff00 5*ffff80 7fff00 7c1f00 300600 100400
  //   contents of rom_23 (hex, n*v repeats v):
  //   9*0 3e000 ff800 1ffc00 3ffe00 7fff00 7fff00 5*ffff80 7fff00 7fff00 3ffe00 1c1c00 c1800
  //   contents of rom_24 (hex, n*v repeats v):
  //   8*0 3e000 ff800 1ffc00 3ffe00 7fff00 7fff00 5*ffff80 7fff00 7fff00 3ffe00 1ffc00 ff800 3e000
  //   contents of rom_25 (hex, n*v repeats v):
  //   7*0 3e000 ff800 1ffc00 3ffe00 7fff00 7fff00 5*ffff80 7fff00 7fff00 3ffe00 1ffc00 ff800 3e000
  //   contents of rom_26 (hex, n*v repeats v):
  //   6*0 3e000 ff800 1ffc00 3ffe00 7fff00 7fff00 5*ffff80 7fff00 7fff00 3ffe00 1ffc00 ff800 3e000
  //   contents of rom_27 (hex, n*v repeats v):
  //   5*0 3e000 ff800 1ffc00 3ffe00 7fff00 7fff00 5*ffff80 7fff00 7fff00 3ffe00 1ffc00 ff800 3e000
  //   contents of rom_28 (hex, n*v repeats v):
  //   4*0 3e000 ff800 1ffc00 3ffe00 7fff00 7fff00 5*ffff80 7fff00 7fff00 3ffe00 1ffc00 ff800 3e000
  //   contents of rom_29 (hex, n*v repeats v):
  //   0 0 0 3e000 ff800 1ffc00 3ffe00 7fff00 7fff00 5*ffff80 7fff00 7fff00 3ffe00 1ffc00 ff800 3e000
  //   contents of rom_30 (hex, n*v repeats v):
  //   0 0 3e000 ff800 1ffc00 3ffe00 7fff00 7fff00 5*ffff80 7fff00 7fff00 3ffe00 1ffc00 ff800 3e000
  //   contents of rom_31 (hex, n*v repeats v):
  //   0 3e000 ff800 1ffc00 3ffe00 7fff00 7fff00 5*ffff80 7fff00 7fff00 3ffe00 1ffc00 ff800 3e000
endmodule
