// Logisim project Hipnotizador.circ as structural Verilog: 1 circuit, main circuit main
// a
module main (
);

  wire clock_1_out, INVERSOR, t_ff_1_q;
  wire [2:0] counter_1_q;
  wire [26:0] a, b, c, d, e, f, g, h, i, j, k, l, m, x;

  Button button_1 (.out(INVERSOR));
  T_Flip_Flop t_ff_1 (.clk(INVERSOR), .T(1'b1), .Q(t_ff_1_q));  // open: Qn, preset, reset, en
  Clock clock_1 (.out(clock_1_out));
  Counter #(.width(3), .max('h3)) counter_1 (
    .load(t_ff_1_q), .Q(counter_1_q), .clk(clock_1_out));  // open: D, count, carry, clr
  DotMatrix #(.matrixcols(27), .matrixrows(27)) dotmatrix_1 (
    .col0(a), .col1(b), .col2(c), .col3(d), .col4(e), .col5(f), .col6(g), .col7(h), .col8(i), .col9(j),
    .col10(k), .col11(l), .col12(m), .col13(x), .col14(m), .col15(l), .col16(k), .col17(j), .col18(i),
    .col19(h), .col20(g), .col21(f), .col22(e), .col23(d), .col24(c), .col25(b), .col26(a));
  ROM #(.addrWidth(3), .dataWidth(27)) rom_1 (.addr(counter_1_q), .data(a));  // open: sel
  ROM #(.addrWidth(3), .dataWidth(27)) rom_2 (.addr(counter_1_q), .data(b));  // open: sel
  ROM #(.addrWidth(3), .dataWidth(27)) rom_3 (.addr(counter_1_q), .data(c));  // open: sel
  ROM #(.addrWidth(3), .dataWidth(27)) rom_4 (.addr(counter_1_q), .data(d));  // open: sel
  ROM #(.addrWidth(3), .dataWidth(27)) rom_5 (.addr(counter_1_q), .data(e));  // open: sel
  ROM #(.addrWidth(3), .dataWidth(27)) rom_6 (.addr(counter_1_q), .data(f));  // open: sel
  ROM #(.addrWidth(3), .dataWidth(27)) rom_7 (.addr(counter_1_q), .data(g));  // open: sel
  ROM #(.addrWidth(3), .dataWidth(27)) rom_8 (.addr(counter_1_q), .data(h));  // open: sel
  ROM #(.addrWidth(3), .dataWidth(27)) rom_9 (.addr(counter_1_q), .data(i));  // open: sel
  ROM #(.addrWidth(3), .dataWidth(27)) rom_10 (.addr(counter_1_q), .data(j));  // open: sel
  ROM #(.addrWidth(3), .dataWidth(27)) rom_11 (.addr(counter_1_q), .data(k));  // open: sel
  ROM #(.addrWidth(3), .dataWidth(27)) rom_12 (.addr(counter_1_q), .data(l));  // open: sel
  ROM #(.addrWidth(3), .dataWidth(27)) rom_13 (.addr(counter_1_q), .data(m));  // open: sel
  ROM #(.addrWidth(3), .dataWidth(27)) rom_14 (.addr(counter_1_q), .data(x));  // open: sel

  // Notes on the sheet:
  //   contents of rom_1 (hex, n*v repeats v):
  //   4200021 43fe10 8c0188 1100044
  //   contents of rom_2 (hex, n*v repeats v):
  //   43fe10 8c0188 1100044 2200022
  //   contents of rom_3 (hex, n*v repeats v):
  //   8c0188 1100044 2200022 440f811
  //   contents of rom_4 (hex, n*v repeats v):
  //   1100044 2200022 440f811 830608
  //   contents of rom_5 (hex, n*v repeats v):
  //   2200022 440f811 830608 1040104
  //   contents of rom_6 (hex, n*v repeats v):
  //   440f811 830608 1040104 2080082
  //   contents of rom_7 (hex, n*v repeats v):
  //   830608 1040104 2080082 4107041
  //   contents of rom_8 (hex, n*v repeats v):
  //   1040104 2080082 4107041 218c20
  //   contents of rom_9 (hex, n*v repeats v):
  //   1080084 2107042 4218c21 420210
  //   contents of rom_10 (hex, n*v repeats v):
  //   2107044 4208821 420210 840108
  //   contents of rom_11 (hex, n*v repeats v):
  //   2108842 4210421 440110 887088
  //   contents of rom_12 (hex, n*v repeats v):
  //   2210422 4420211 842108 1088884
  //   contents of rom_13 (hex, n*v repeats v):
  //   2220222 4442111 885088 1110444
  //   contents of rom_14 (hex, n*v repeats v):
  //   2222222 4445111 888888 1110444
endmodule
