// Logisim project Jogo.circ as structural Verilog: 1 circuit, main circuit main
module main (
);

  wire _1, _2, _3, _4, _5, _6, _7, _8, and_1_out, and_2_out, and_3_out, and_4_out, and_5_out, and_6_out,
       and_7_out, and_8_out, clock, clock_1_out, counter_1_carry, counter_2_carry;
  wire [2:0] random_1_out;
  wire [3:0] counter_1_q, counter_2_q;
  wire [27:0] a, b, c, d, e, f, g, h, i;

  Clock clock_1 (.out(clock_1_out));
  Random #(.width(3)) random_1 (.clk(clock_1_out), .out(random_1_out));  // open: next, clr
  ROM #(.addrWidth(3), .dataWidth(28)) rom_1 (.addr(random_1_out), .data(a));  // open: sel
  ROM #(.addrWidth(3), .dataWidth(28)) rom_2 (.addr(random_1_out), .data(b));  // open: sel
  ROM #(.addrWidth(3), .dataWidth(28)) rom_3 (.addr(random_1_out), .data(c));  // open: sel
  ROM #(.addrWidth(3), .dataWidth(28)) rom_4 (.addr(random_1_out), .data(d));  // open: sel
  ROM #(.addrWidth(3), .dataWidth(28)) rom_5 (.addr(random_1_out), .data(e));  // open: sel
  ROM #(.addrWidth(3), .dataWidth(28)) rom_6 (.addr(random_1_out), .data(f));  // open: sel
  ROM #(.addrWidth(3), .dataWidth(28)) rom_7 (.addr(random_1_out), .data(g));  // open: sel
  ROM #(.addrWidth(3), .dataWidth(28)) rom_8 (.addr(random_1_out), .data(h));  // open: sel
  ROM #(.addrWidth(3), .dataWidth(28)) rom_9 (.addr(random_1_out), .data(i));  // open: sel
  DotMatrix #(.matrixcols(28), .matrixrows(28)) dotmatrix_1 (
    .col0({28{1'b1}}), .col1(28'h8040201), .col2(a), .col3(b), .col4(c), .col5(c), .col6(b), .col7(a),
    .col8(28'h8040201), .col9({28{1'b1}}), .col10(28'h8066601), .col11(d), .col12(e), .col13(f), .col14(f),
    .col15(e), .col16(d), .col17(28'h8066601), .col18({28{1'b1}}), .col19(28'h8040201), .col20(g), .col21(h),
    .col22(i), .col23(i), .col24(h), .col25(g), .col26(28'h8040201), .col27({28{1'b1}}));
  and and_1 (and_1_out, a[6], _3);
  and and_2 (and_2_out, a[15], _2);
  and and_3 (and_3_out, a[21], _1);
  or or_1 (clock, and_3_out, and_2_out, and_1_out, and_5_out, and_4_out, and_8_out, and_7_out, and_6_out);
  Button button_1 (.out(_1));
  Button button_2 (.out(_2));
  Button button_3 (.out(_3));
  Counter #(.width(4), .max('ha)) counter_1 (
    .Q(counter_1_q), .carry(counter_1_carry), .clk(clock), .clr(counter_1_carry));  // open: load, D, count
  and and_4 (and_4_out, d[6], _5);
  and and_5 (and_5_out, d[21], _4);
  Button button_4 (.out(_4));
  Button button_5 (.out(_5));
  Hex_Digit_Display hex_digit_display_1 (.value(counter_2_q));  // open: dp
  Hex_Digit_Display hex_digit_display_2 (.value(counter_1_q));  // open: dp
  Counter #(.width(4), .max('ha)) counter_2 (
    .Q(counter_2_q), .carry(counter_2_carry), .clk(counter_1_carry), .clr(counter_2_carry));  // open: load, D, count
  and and_6 (and_6_out, g[7], _8);
  and and_7 (and_7_out, g[15], _7);
  and and_8 (and_8_out, g[21], _6);
  Button button_6 (.out(_6));
  Button button_7 (.out(_7));
  Button button_8 (.out(_8));

  // Notes on the sheet:
  //   contents of rom_1 (hex, n*v repeats v):
  //   b240201 8059201 80402c9 5*8040201
  //   contents of rom_2 (hex, n*v repeats v):
  //   9140201 8048a01 8040245 5*8040201
  //   contents of rom_3 (hex, n*v repeats v):
  //   8140201 8040a01 8040205 5*8040201
  //   contents of rom_4 (hex, n*v repeats v):
  //   6*8056a01 8056ac9 b256a01
  //   contents of rom_5 (hex, n*v repeats v):
  //   6*804f201 804f245 914f201
  //   contents of rom_6 (hex, n*v repeats v):
  //   6*807fe01 807fe05 817fe01
  //   contents of rom_7 (hex, n*v repeats v):
  //   8040201 8040201 8040201 b240201 8059201 80402c9 8040201 8040201
  //   contents of rom_8 (hex, n*v repeats v):
  //   8040201 8040201 8040201 9140201 8048a01 8040245 8040201 8040201
  //   contents of rom_9 (hex, n*v repeats v):
  //   8040201 8040201 8040201 8140201 8040a01 8040205 8040201 8040201
endmodule
