// Logisim project Jogo2.circ as structural Verilog: 1 circuit, main circuit main
module main (
);

  wire and_1_out, and_2_out, and_3_out, and_4_out, and_5_out, and_6_out, and_7_out, and_8_out, and_10_out,
       and_11_out, clock_1_out, clock_2_out, \colisão , counter_2_carry, counter_3_carry, game_over, left,
       not_1_out, not_2_out, not_3_out, not_4_out, or_1_out, right;
  wire [1:0] A, B, C, D, E, F, G, H;
  wire [2:0] counter_1_q, counter_4_q, counter_5_q, random_1_out;
  wire [3:0] counter_2_q, counter_3_q;
  wire [7:0] a_t, b_t, c_t, d_t, e_t, f_t, g_t, h_t, rom_1_data;

  // NOT_Gate not_1 has open pins: in=open, out=not_1_out
  not not_2 (not_2_out, game_over);
  Counter #(.width(3), .max('h7)) counter_1 (
    .count(not_2_out), .Q(counter_1_q), .clk(clock_1_out));  // open: load, D, carry, clr
  Clock clock_1 (.out(clock_1_out));
  Button button_1 (.out(left));
  Button button_2 (.out(right));
  ROM #(.addrWidth(3)) rom_1 (.addr(counter_1_q), .data(rom_1_data));  // open: sel
  DotMatrix #(.matrixcols(8), .matrixrows(8)) dotmatrix_1 (
    .col0(a_t), .col1(b_t), .col2(c_t), .col3(d_t), .col4(e_t), .col5(f_t), .col6(g_t), .col7(h_t));
  DotMatrix #(.matrixcols(8), .matrixrows(2)) dotmatrix_2 (
    .col0(A), .col1(B), .col2(C), .col3(D), .col4(E), .col5(F), .col6(G), .col7(H));
  Demultiplexer #(.select(3), .width(8)) demultiplexer_1 (
    .out0(a_t), .out1(b_t), .out2(c_t), .out3(d_t), .out4(e_t), .out5(f_t), .out6(g_t), .out7(h_t),
    .in(rom_1_data), .sel(random_1_out));  // open: en
  Random #(.width(3)) random_1 (.clk(rom_1_data[7]), .out(random_1_out));  // open: next, clr
  Hex_Digit_Display hex_digit_display_1 (.value(counter_3_q));  // open: dp
  Hex_Digit_Display hex_digit_display_2 (.value(counter_2_q));  // open: dp
  Counter #(.width(4), .max('ha)) counter_2 (
    .Q(counter_2_q), .carry(counter_2_carry), .clk(counter_3_carry), .clr(counter_2_carry));  // open: load, D, count
  Counter #(.width(4), .max('ha)) counter_3 (
    .Q(counter_3_q), .carry(counter_3_carry), .clk(\colisão ), .clr(counter_3_carry));  // open: load, D, count
  Demultiplexer #(.select(3), .width(2)) demultiplexer_2 (
    .out0(A), .out1(B), .out2(C), .out3(D), .out4(E), .out5(F), .out6(G), .out7(H), .in(2'b11),
    .sel(counter_4_q));  // open: en
  and and_1 (and_1_out, or_1_out, ~game_over);  // AND_Gate
  or or_1 (or_1_out, left, right);
  and and_2 (and_2_out, B[0], b_t[0]);
  and and_3 (and_3_out, A[0], a_t[0]);
  not not_3 (not_3_out, game_over);
  Clock clock_2 (.out(clock_2_out));
  Counter #(.width(3), .max('h7)) counter_4 (
    .load(left), .Q(counter_4_q), .clk(and_1_out));  // open: D, count, carry, clr
  and and_4 (and_4_out, C[0], c_t[0]);
  Counter #(.width(3), .max('h7)) counter_5 (
    .count(not_3_out), .Q(counter_5_q), .clk(clock_2_out));  // open: load, D, carry, clr
  and and_5 (and_5_out, D[0], d_t[0]);
  and and_6 (and_6_out, counter_5_q[0], counter_5_q[1], counter_5_q[2]);
  and and_7 (and_7_out, F[0], f_t[0]);
  and and_8 (and_8_out, E[0], e_t[0]);
  and and_9 (game_over, and_6_out, ~\colisão );  // AND_Gate
  and and_10 (and_10_out, G[0], g_t[0]);
  and and_11 (and_11_out, H[0], h_t[0]);
  or or_2 (\colisão , and_11_out, and_10_out, and_7_out, and_8_out, and_5_out, and_4_out, and_2_out, and_3_out);
  // NOT_Gate not_4 has open pins: in=open, out=not_4_out

  // Notes on the sheet:
  //   botões
  //   esqueda // direita
  //   andamento do bloquinho verde
  //   contents of rom_1 (hex, n*v repeats v):
  //   80 40 20 10 8 4 2 1
  //   contador 
  //   circuito para fazer os botões funcionarem
endmodule
