// Logisim project Maça.circ as structural Verilog: 1 circuit, main circuit main
module main (
);

  wire and_1_out, and_2_out, button_1_out, clock_1_out, clock_2_out, tunnel, tunnel_t;
  wire [2:0] counter_1_q;
  wire [3:0] counter_2_q;
  wire [19:0] _3, _4, _5, _6, _7, _8, _9, _10, _11, _12, a, c, n, p0, p1, p2, p3, p4, p5, p6, p7, p8, p9,
       p10, p11, p12, p13, p14;

  and and_1 (and_1_out, clock_1_out, tunnel_t);
  Clock clock_1 (.out(clock_1_out));
  Button button_1 (.out(button_1_out));
  Counter #(.width(3), .max('h6), .ongoal("stay")) counter_1 (
    .Q(counter_1_q), .clk(and_1_out), .clr(tunnel));  // open: load, D, count, carry
  T_Flip_Flop t_ff_1 (.clk(button_1_out), .T(1'b1), .Q(tunnel_t), .Qn(tunnel));  // open: preset, reset, en
  Multiplexer #(.select(3), .width(20)) multiplexer_1 (
    .in0({p0[19:10], 4'b0000, p0[5:0]}), .in1({p0[19:10], 4'b0000, p0[5:0]}),
    .in2({p7[19:6], 2'b00, p7[3:0]}), .in3({p11[19:6], 2'b00, p11[3:0]}), .out(_3), .sel(counter_1_q));  // open: in4, in5, in6, in7, en
  Multiplexer #(.select(3), .width(20)) multiplexer_2 (
    .in0({p1[19:11], {7{1'b0}}, p1[3:0]}), .in1({p1[19:11], {7{1'b0}}, p1[3:0]}),
    .in2({p8[19:7], 4'b0000, p8[2:0]}), .in3({p12[19:7], 4'b0000, p12[2:0]}), .out(_4), .sel(counter_1_q));  // open: in4, in5, in6, in7, en
  Multiplexer #(.select(3), .width(20)) multiplexer_3 (
    .in0({p2[19:12], {9{1'b0}}, p2[2:0]}), .in1({p2[19:12], {9{1'b0}}, p2[2:0]}),
    .in2({p8[19:7], 4'b0000, p8[2:0]}), .in3({p13[19:6], 3'b000, p13[2:0]}), .out(_5), .sel(counter_1_q));  // open: in4, in5, in6, in7, en
  Multiplexer #(.select(3), .width(20)) multiplexer_4 (
    .in0({p2[19:12], {9{1'b0}}, p2[2:0]}), .in1({p2[19:12], {9{1'b0}}, p2[2:0]}),
    .in2({p9[19:8], 4'b0000, p9[3:0]}), .in3({p14[19:5], 1'b0, p14[3:0]}), .out(_6), .sel(counter_1_q));  // open: in4, in5, in6, in7, en
  Multiplexer #(.select(3), .width(20)) multiplexer_5 (
    .in0({p3[19:12], {8{1'b0}}, p3[3:0]}), .in1({p3[19:12], {8{1'b0}}, p3[3:0]}),
    .in2({p9[19:8], 4'b0000, p9[3:0]}), .out(_7), .sel(counter_1_q));  // open: in3, in4, in5, in6, in7, en
  Multiplexer #(.select(3), .width(20)) multiplexer_6 (
    .in0({p3[19:12], {8{1'b0}}, p3[3:0]}), .in1({p4[19:8], 4'b0000, p4[3:0]}),
    .in2({p8[19:7], 4'b0000, p8[2:0]}), .out(_8), .sel(counter_1_q));  // open: in3, in4, in5, in6, in7, en
  DotMatrix #(.matrixcols(20), .matrixrows(20)) dotmatrix_1 (
    .col0(a), .col1(a), .col2(a), .col3(a), .col4(c), .col5(_3), .col6(_4), .col7(_5), .col8(_6), .col9(_7),
    .col10(_8), .col11(_9), .col12(_10), .col13(_11), .col14(_12), .col15(n), .col16(a), .col17(a),
    .col18(a), .col19(a));
  Multiplexer #(.select(3), .width(20)) multiplexer_7 (
    .in0({p2[19:12], {9{1'b0}}, p2[2:0]}), .in1({p5[19:7], 4'b0000, p5[2:0]}),
    .in2({p10[19:6], 3'b000, p10[2:0]}), .out(_9), .sel(counter_1_q));  // open: in3, in4, in5, in6, in7, en
  Multiplexer #(.select(3), .width(20)) multiplexer_8 (
    .in0({p2[19:12], {9{1'b0}}, p2[2:0]}), .in1({p6[19:6], 3'b000, p6[2:0]}),
    .in2({p7[19:6], 2'b00, p7[3:0]}), .out(_10), .sel(counter_1_q));  // open: in3, in4, in5, in6, in7, en
  Multiplexer #(.select(3), .width(20)) multiplexer_9 (
    .in0({p1[19:11], {7{1'b0}}, p1[3:0]}), .in1({p7[19:6], 2'b00, p7[3:0]}), .out(_11), .sel(counter_1_q));  // open: in2, in3, in4, in5, in6, in7, en
  Multiplexer #(.select(3), .width(20)) multiplexer_10 (
    .in0({p0[19:10], 4'b0000, p0[5:0]}), .out(_12), .sel(counter_1_q));  // open: in1, in2, in3, in4, in5, in6, in7, en
  and and_2 (and_2_out, clock_2_out, tunnel_t);
  Clock clock_2 (.out(clock_2_out));
  Counter #(.width(4), .max('h6), .ongoal("stay")) counter_2 (
    .Q(counter_2_q), .clk(and_2_out), .clr(tunnel));  // open: load, D, count, carry
  ROM #(.addrWidth(4), .dataWidth(20)) rom_1 (.addr(counter_2_q), .data(a));  // open: sel
  ROM #(.addrWidth(4), .dataWidth(20)) rom_2 (.addr(counter_2_q), .data(c));  // open: sel
  ROM #(.addrWidth(4), .dataWidth(20)) rom_3 (.addr(counter_2_q), .data(_3));  // open: sel
  ROM #(.addrWidth(4), .dataWidth(20)) rom_4 (.addr(counter_2_q), .data(_4));  // open: sel
  ROM #(.addrWidth(4), .dataWidth(20)) rom_5 (.addr(counter_2_q), .data(_5));  // open: sel
  ROM #(.addrWidth(4), .dataWidth(20)) rom_6 (.addr(counter_2_q), .data(_6));  // open: sel
  ROM #(.addrWidth(4), .dataWidth(20)) rom_7 (.addr(counter_2_q), .data(_7));  // open: sel
  ROM #(.addrWidth(4), .dataWidth(20)) rom_8 (.addr(counter_2_q), .data(_8));  // open: sel
  ROM #(.addrWidth(4), .dataWidth(20)) rom_9 (.addr(counter_2_q), .data(_9));  // open: sel
  ROM #(.addrWidth(4), .dataWidth(20)) rom_10 (.addr(counter_2_q), .data(_10));  // open: sel
  ROM #(.addrWidth(4), .dataWidth(20)) rom_11 (.addr(counter_2_q), .data(_11));  // open: sel
  ROM #(.addrWidth(4), .dataWidth(20)) rom_12 (.addr(counter_2_q), .data(_12));  // open: sel
  ROM #(.addrWidth(4), .dataWidth(20)) rom_13 (.addr(counter_2_q), .data(n));  // open: sel

  // Other names for the same wires on the sheet: d[19:0] = _3; e[19:0] = _4; f[19:0] = _5; g[19:0] = _6; h[19:0] = _7;
  //   i[19:0] = _8; j[19:0] = _9; k[19:0] = _10; l[19:0] = _11; m[19:0] = _12

  // Notes on the sheet:
  //   contents of rom_2 (hex, n*v repeats v):
  //   3c0 3c0 70 70
  //   contents of rom_3 (hex, n*v repeats v):
  //   7f0 7f0 78 78
  //   contents of rom_4 (hex, n*v repeats v):
  //   e78 e78 fc fc
  //   contents of rom_5 (hex, n*v repeats v):
  //   1c7c 1c7c fc fc
  //   contents of rom_6 (hex, n*v repeats v):
  //   1dfc 1dfc 1f8 38
  //   contents of rom_7 (hex, n*v repeats v):
  //   1ff8 1ff8 3f8 18
  //   contents of rom_8 (hex, n*v repeats v):
  //   7ff8 7ff8 10fc 800
  //   contents of rom_9 (hex, n*v repeats v):
  //   dffc c0fc 307c c00
  //   contents of rom_10 (hex, n*v repeats v):
  //   1ffc 7c 2078 400
  //   contents of rom_11 (hex, n*v repeats v):
  //   ff8 78 70 0 c0 3 2
  //   contents of rom_12 (hex, n*v repeats v):
  //   7f0 70 0 0 60 6 3
  //   contents of rom_13 (hex, n*v repeats v):
  //   3c0 5*0 1
endmodule
