// Logisim project Nome.circ as structural Verilog: 1 circuit, main circuit main
module main (
);

  wire clock_1_out;
  wire [5:0] a, aa, b, bb, c, cc, counter_1_q, d, dd, e, ee, f, ff, g, h, i, j, k, l, m, n, o, p, q, r,
       rom_1_data, s, t, u, v, w, x, y, z;

  Counter #(.width(6), .max('h3a)) counter_1 (.Q(counter_1_q), .clk(clock_1_out));  // open: load, D, count, carry, clr
  Clock clock_1 (.out(clock_1_out));
  DotMatrix #(.matrixcols(32), .matrixrows(6)) dotmatrix_1 (
    .col0(ff), .col1(ee), .col2(dd), .col3(cc), .col4(bb), .col5(aa), .col6(z), .col7(y), .col8(x), .col9(w),
    .col10(v), .col11(u), .col12(t), .col13(s), .col14(r), .col15(q), .col16(p), .col17(o), .col18(n),
    .col19(m), .col20(l), .col21(k), .col22(j), .col23(i), .col24(h), .col25(g), .col26(f), .col27(e),
    .col28(d), .col29(c), .col30(b), .col31(a));
  ROM #(.addrWidth(6), .dataWidth(6)) rom_1 (.addr(counter_1_q), .data(rom_1_data));  // open: sel
  Shift_Register #(.width(6), .length(32)) shift_register_1 (
    .in(rom_1_data), .clk(clock_1_out), .q0(a), .q1(b), .q2(c), .q3(d), .q4(e), .q5(f), .q6(g), .q7(h),
    .q8(i), .q9(j), .q10(k), .q11(l), .q12(m), .q13(n), .q14(o), .q15(p), .q16(q), .q17(r), .q18(s), .q19(t),
    .q20(u), .q21(v), .q22(w), .q23(x), .q24(y), .q25(z), .q26(aa), .q27(bb), .q28(cc), .q29(dd), .q30(ee),
    .q31(ff));  // open: shift, out, load, clr, d0, d1, d2, d3, d4, d5, d6, d7, d8, d9, d10, d11, d12, d13, d14, d15, d16, d17, d18, d19, d20, d21, d22, d23, d24, d25, d26, d27, d28, d29, d30, d31

  // Notes on the sheet:
  //   contents of rom_1 (hex, n*v repeats v):
  //   21 21 3f 20 20 0 3f 21 21 21 3f 0 3f 24 24 24 3f 0 3f 21 21 21 3f
endmodule
