// Logisim project Relogio.circ as structural Verilog: 5 circuits, main circuit main
module main (
);

  wire _6_out, _9_2_out, _9_out, a, a1, a2, aa, b, b1, b2, bb, c, c1, c2, cc, d, d1, d2, dd, e, e1, e2, ee,
       f, f1, f2, ff, g, g1, g2, gg, Q1, Q2, Q3, Q4, Q11, Q22, Q33, Q44, unidade_de_minutos_1_out_1,
       unidade_de_minutos_1_out_4, z;

  nand _9 (_9_out, unidade_de_minutos_1_out_1, unidade_de_minutos_1_out_4);
  UNIDADE_DE_MINUTOS unidade_de_minutos_1 (
    .out_1(unidade_de_minutos_1_out_1), .out_4(unidade_de_minutos_1_out_4), .out_5(a), .out_6(b), .out_7(c),
    .out_8(d), .out_9(e), .out_10(f), .out_11(g));  // open: out_2, out_3
  nand _9_2 (_9_2_out, Q11, Q33);
  and and_1 (z, Q22, g2);
  DEZENA_DE_MINUTOS dezena_de_minutos_1 (
    .in_1(_9_out), .out_2(Q1), .out_3(Q2), .out_4(Q3), .out_5(Q4), .out_6(aa), .out_7(bb), .out_8(cc),
    .out_9(dd), .out_10(ee), .out_11(ff), .out_12(gg));
  nand _6 (_6_out, Q2, Q3);
  DEZENA_DE_HORAS dezena_de_horas_1 (
    .in_1(_9_2_out), .in_2(z), .out_3(a2), .out_4(b2), .out_5(c2), .out_6(d2), .out_7(e2), .out_8(f2),
    .out_9(g2));
  UNIDADE_DE_HORAS unidade_de_horas_1 (
    .in_1(_6_out), .in_2(z), .out_4(Q11), .out_5(Q22), .out_6(Q33), .out_7(Q44), .out_3(a1), .out_8(b1),
    .out_9(c1), .out_10(d1), .out_11(e1), .out_12(f1), .out_13(g1));
  _7_Segment_Display u_7_segment_display_1 (.g(g2), .f(f2), .a(a2), .b(b2), .e(e2), .d(d2), .c(c2));  // open: dp
  _7_Segment_Display u_7_segment_display_2 (.g(g1), .f(f1), .a(a1), .b(b1), .e(e1), .d(d1), .c(c1));  // open: dp
  LED led_1 ();  // open: in
  LED led_2 ();  // open: in
  _7_Segment_Display u_7_segment_display_3 (.g(g), .f(f), .a(a), .b(b), .e(e), .d(d), .c(c));  // open: dp
  _7_Segment_Display u_7_segment_display_4 (.g(gg), .f(ff), .a(aa), .b(bb), .e(ee), .d(dd), .c(cc));  // open: dp

  // Notes on the sheet:
  //   entradas do circuito
  //   de unidade de horas
  //   saidas do circuito
  //   CIRCUITO DO DISPLAY
  //   DA DEZENA DE MINUTOS  ->
  //   entradas do circuito
  //   de minutos
  //   CIRCUITO DO DISPLAY
  //   <- DA UNIDADE DE MINUTOS
  //   Contador de número 3
  //   zerador das horas
  //   quando der 24 horas
  //   saidas do circuito
  //   da dezena de minutos
  //   saidas do circuito
  //   de unidade de horas
  //   CIRCUITO DO DISPLAY
  //   <- DA UNIDADE DE HORAS
  //   CIRCUITO DO DISPLAY
  //   <- DA DEZENA DE HORAS
  //   RELÓGIO DIGITAL
  //   EM FUNÇÃO DA UNIDADE DE MINUTOS
endmodule

module UNIDADE_DE_MINUTOS (
  output out_1,
  output out_2,
  output out_3,
  output out_4,
  output out_5,
  output out_6,
  output out_7,
  output out_8,
  output out_9,
  output out_10,
  output out_11
);

  wire and_1_out, and_2_out, and_3_out, and_4_out, and_5_out, and_6_out, and_7_out, and_8_out, and_9_out,
       and_10_out, and_11_out, and_12_out, and_13_out, clock_1_out, j_k_ff_4_qn, not_1_out, not_2_out,
       not_3_out, xnor_1_out, xnor_2_out, xor_1_out;

  not not_1 (not_1_out, out_3);
  not not_2 (not_2_out, out_2);
  not not_3 (not_3_out, out_1);
  xnor xnor_1 (xnor_1_out, out_3, out_1);
  xnor xnor_2 (xnor_2_out, out_2, out_1);
  and and_1 (and_1_out, not_1_out, not_3_out);
  and and_2 (and_2_out, not_1_out, out_2);
  and and_3 (and_3_out, out_2, not_3_out);
  and and_4 (and_4_out, out_3, not_2_out, out_1);
  and and_5 (and_5_out, not_1_out, not_3_out);
  and and_6 (and_6_out, out_2, not_3_out);
  and and_7 (and_7_out, not_2_out, not_3_out);
  and and_8 (and_8_out, out_3, not_2_out);
  and and_9 (and_9_out, out_3, not_3_out);
  xor xor_1 (xor_1_out, out_3, out_2);
  and and_10 (and_10_out, out_2, not_3_out);
  Clock clock_1 (.out(clock_1_out));
  or or_1 (out_5, xnor_1_out, out_4, out_2);
  or or_2 (out_6, xnor_2_out, not_1_out);
  or or_3 (out_7, out_3, not_2_out, out_1);
  or or_4 (out_8, out_4, and_1_out, and_2_out, and_3_out, and_4_out);
  or or_5 (out_9, and_5_out, and_6_out);
  or or_6 (out_10, out_4, and_7_out, and_8_out, and_9_out);
  or or_7 (out_11, out_4, xor_1_out, and_10_out);
  J_K_Flip_Flop j_k_ff_1 (.J(1'b1), .clk(clock_1_out), .K(1'b1), .Q(out_1));  // open: Qn, preset, en, reset
  and and_11 (and_11_out, j_k_ff_4_qn, out_1);
  J_K_Flip_Flop j_k_ff_2 (.J(and_11_out), .clk(clock_1_out), .K(out_1), .Q(out_2));  // open: Qn, preset, en, reset
  and and_12 (and_12_out, out_2, out_1);
  J_K_Flip_Flop j_k_ff_3 (.J(and_12_out), .clk(clock_1_out), .K(and_12_out), .Q(out_3));  // open: Qn, preset, en, reset
  and and_13 (and_13_out, out_3, and_12_out);
  J_K_Flip_Flop j_k_ff_4 (
    .J(and_13_out), .clk(clock_1_out), .K(out_1), .Q(out_4), .Qn(j_k_ff_4_qn));  // open: preset, en, reset

  // Other names for the same wires on the sheet: A = out_4; B = out_3; C = out_2; D = out_1

  // Notes on the sheet:
  //   DECODIFICADOR DE 7 SEGMENTOS
  //   CONTADOR DE 0 A 9
endmodule

module DEZENA_DE_MINUTOS (
  input  in_1,
  output out_2,
  output out_3,
  output out_4,
  output out_5,
  output out_6,
  output out_7,
  output out_8,
  output out_9,
  output out_10,
  output out_11,
  output out_12
);

  wire _6_out, and_1_out, and_2_out, and_3_out, and_4_out, and_5_out, and_6_out, and_7_out, and_8_out,
       and_9_out, and_10_out, and_11_out, and_12_out, and_13_out, j_k_ff_4_qn, not_1_out, not_2_out,
       not_3_out, xnor_1_out, xnor_2_out, xor_1_out;

  not not_1 (not_1_out, out_4);
  not not_2 (not_2_out, out_3);
  J_K_Flip_Flop j_k_ff_1 (.J(1'b1), .clk(in_1), .K(1'b1), .Q(out_2));  // open: Qn, preset, en, reset
  not not_3 (not_3_out, out_2);
  and and_1 (and_1_out, j_k_ff_4_qn, out_2);
  and and_2 (and_2_out, out_3, out_2);
  J_K_Flip_Flop j_k_ff_2 (.J(and_1_out), .clk(in_1), .K(out_2), .Q(out_3), .reset(_6_out));  // open: Qn, preset, en
  and _6 (_6_out, out_4, out_3);
  xnor xnor_1 (xnor_1_out, out_4, out_2);
  xnor xnor_2 (xnor_2_out, out_3, out_2);
  and and_3 (and_3_out, not_1_out, not_3_out);
  and and_4 (and_4_out, not_1_out, out_3);
  and and_5 (and_5_out, out_3, not_3_out);
  and and_6 (and_6_out, out_4, not_2_out, out_2);
  and and_7 (and_7_out, not_1_out, not_3_out);
  and and_8 (and_8_out, out_3, not_3_out);
  and and_9 (and_9_out, not_2_out, not_3_out);
  and and_10 (and_10_out, out_4, not_2_out);
  and and_11 (and_11_out, out_4, not_3_out);
  xor xor_1 (xor_1_out, out_4, out_3);
  and and_12 (and_12_out, out_3, not_3_out);
  J_K_Flip_Flop j_k_ff_3 (.J(and_2_out), .clk(in_1), .K(and_2_out), .Q(out_4), .reset(_6_out));  // open: Qn, preset, en
  and and_13 (and_13_out, out_4, and_2_out);
  or or_1 (out_6, xnor_1_out, out_5, out_3);
  or or_2 (out_7, xnor_2_out, not_1_out);
  or or_3 (out_8, out_4, not_2_out, out_2);
  or or_4 (out_9, out_5, and_3_out, and_4_out, and_5_out, and_6_out);
  or or_5 (out_10, and_7_out, and_8_out);
  or or_6 (out_11, out_5, and_9_out, and_10_out, and_11_out);
  or or_7 (out_12, out_5, xor_1_out, and_12_out);
  J_K_Flip_Flop j_k_ff_4 (
    .J(and_13_out), .clk(in_1), .K(out_2), .Q(out_5), .Qn(j_k_ff_4_qn));  // open: preset, en, reset

  // Other names for the same wires on the sheet: A = out_5; B = out_4; C = out_3; D = out_2

  // Notes on the sheet:
  //   ENTRADA DO SINAL
  //   DO CIRCUITO DE SEGUNDOS
  //   DECODIFICADOR DE 7 SEGMENTOS
  //   CONTADOR DE 0 A 6
endmodule

module UNIDADE_DE_HORAS (
  input  in_1,
  input  in_2,
  output out_3,
  output out_4,
  output out_5,
  output out_6,
  output out_7,
  output out_8,
  output out_9,
  output out_10,
  output out_11,
  output out_12,
  output out_13
);

  wire _10_out, and_1_out, and_2_out, and_3_out, and_4_out, and_5_out, and_6_out, and_7_out, and_8_out,
       and_9_out, and_10_out, not_1_out, not_2_out, not_3_out, or_8_out, xnor_1_out, xnor_2_out, xor_1_out;

  not not_1 (not_1_out, out_5);
  not not_2 (not_2_out, out_6);
  not not_3 (not_3_out, out_7);
  xnor xnor_1 (xnor_1_out, out_5, out_7);
  xnor xnor_2 (xnor_2_out, out_6, out_7);
  and and_1 (and_1_out, not_1_out, not_3_out);
  and and_2 (and_2_out, not_1_out, out_6);
  and and_3 (and_3_out, out_6, not_3_out);
  and and_4 (and_4_out, out_5, not_2_out, out_7);
  and and_5 (and_5_out, not_1_out, not_3_out);
  and and_6 (and_6_out, out_6, not_3_out);
  and and_7 (and_7_out, not_2_out, not_3_out);
  and and_8 (and_8_out, out_5, not_2_out);
  and and_9 (and_9_out, out_5, not_3_out);
  xor xor_1 (xor_1_out, out_5, out_6);
  and and_10 (and_10_out, out_6, not_3_out);
  or or_1 (out_3, xnor_1_out, out_4, out_6);
  or or_2 (out_8, xnor_2_out, not_1_out);
  or or_3 (out_9, out_5, not_2_out, out_7);
  or or_4 (out_10, out_4, and_1_out, and_2_out, and_3_out, and_4_out);
  or or_5 (out_11, and_5_out, and_6_out);
  or or_6 (out_12, out_4, and_7_out, and_8_out, and_9_out);
  or or_7 (out_13, out_4, xor_1_out, and_10_out);
  T_Flip_Flop #(.trigger("falling")) t_ff_1 (
    .clk(in_1), .T(1'b1), .Q(out_7), .reset(or_8_out));  // open: Qn, preset, en
  T_Flip_Flop #(.trigger("falling")) t_ff_2 (
    .clk(out_7), .T(1'b1), .Q(out_6), .reset(or_8_out));  // open: Qn, preset, en
  or or_8 (or_8_out, in_2, _10_out);
  and _10 (_10_out, out_4, out_6);
  T_Flip_Flop #(.trigger("falling")) t_ff_3 (
    .clk(out_6), .T(1'b1), .Q(out_5), .reset(or_8_out));  // open: Qn, preset, en
  T_Flip_Flop #(.trigger("falling")) t_ff_4 (
    .clk(out_5), .T(1'b1), .Q(out_4), .reset(or_8_out));  // open: Qn, preset, en

  // Other names for the same wires on the sheet: A = out_4; B = out_5; C = out_6; D = out_7

  // Notes on the sheet:
  //   DECODIFICADOR DE 7 SEGMENTOS
endmodule

module DEZENA_DE_HORAS (
  input  in_1,
  input  in_2,
  output out_3,
  output out_4,
  output out_5,
  output out_6,
  output out_7,
  output out_8,
  output out_9
);

  wire A, and_1_out, and_2_out, and_3_out, and_4_out, and_5_out, and_6_out, and_7_out, and_8_out, and_9_out,
       and_10_out, and_11_out, B, not_1_out, not_2_out, not_3_out, or_8_out, t_ff_3_q, xnor_1_out,
       xnor_2_out, xor_1_out;

  not not_1 (not_1_out, 1'b0);
  not not_2 (not_2_out, A);
  not not_3 (not_3_out, B);
  and and_1 (and_1_out, not_1_out, not_3_out);
  and and_2 (and_2_out, not_1_out, A);
  and and_3 (and_3_out, A, not_3_out);
  and and_4 (and_4_out, 1'b0, not_2_out, B);
  and and_5 (and_5_out, not_1_out, not_3_out);
  and and_6 (and_6_out, A, not_3_out);
  and and_7 (and_7_out, not_2_out, not_3_out);
  and and_8 (and_8_out, 1'b0, not_2_out);
  and and_9 (and_9_out, 1'b0, not_3_out);
  and and_10 (and_10_out, A, not_3_out);
  xnor xnor_1 (xnor_1_out, 1'b0, B);
  xnor xnor_2 (xnor_2_out, A, B);
  xor xor_1 (xor_1_out, 1'b0, A);
  or or_1 (out_3, xnor_1_out, 1'b0, A);
  or or_2 (out_4, xnor_2_out, not_1_out);
  or or_3 (out_5, 1'b0, not_2_out, B);
  or or_4 (out_6, 1'b0, and_1_out, and_2_out, and_3_out, and_4_out);
  or or_5 (out_7, and_5_out, and_6_out);
  or or_6 (out_8, 1'b0, and_7_out, and_8_out, and_9_out);
  or or_7 (out_9, 1'b0, xor_1_out, and_10_out);
  T_Flip_Flop #(.trigger("falling")) t_ff_1 (.clk(in_1), .T(1'b1), .Q(B), .reset(or_8_out));  // open: Qn, preset, en
  T_Flip_Flop #(.trigger("falling")) t_ff_2 (.clk(B), .T(1'b1), .Q(A), .reset(or_8_out));  // open: Qn, preset, en
  or or_8 (or_8_out, in_2, and_11_out);
  and and_11 (and_11_out, A, B);
  T_Flip_Flop #(.trigger("falling")) t_ff_3 (
    .clk(A), .T(1'b1), .Q(t_ff_3_q), .reset(or_8_out));  // open: Qn, preset, en
  T_Flip_Flop #(.trigger("falling")) t_ff_4 (.clk(t_ff_3_q), .T(1'b1), .reset(or_8_out));  // open: Q, Qn, preset, en

  // Notes on the sheet:
  //   DECODIFICADOR DE 7 SEGMENTOS
  //   CONTADOR DE 0 A 2
endmodule
