// Logisim project Seminário ROM.circ as structural Verilog: 1 circuit, main circuit main
module main (
  input  E,
  input  F,
  input  G,
  input  H,
  input  A,
  input  B,
  input  C,
  input  D,
  output [6:0] out_9
);

  wire _10_out, clock_1_out;
  wire [3:0] t_ff_1_q;
  wire [6:0] rom_2_data;

  Clock clock_1 (.out(clock_1_out));
  T_Flip_Flop #(.trigger("falling")) t_ff_1 (
    .clk(clock_1_out), .T(1'b1), .Q(t_ff_1_q[0]), .reset(_10_out));  // open: Qn, preset, en
  _7_Segment_Display u_7_segment_display_1 (.g(E), .f(F), .a(G), .b(H), .e(B), .d(C), .c(D));  // open: dp
  T_Flip_Flop #(.trigger("falling")) t_ff_2 (
    .clk(t_ff_1_q[0]), .T(1'b1), .Q(t_ff_1_q[1]), .reset(_10_out));  // open: Qn, preset, en
  T_Flip_Flop #(.trigger("falling")) t_ff_3 (
    .clk(t_ff_1_q[1]), .T(1'b1), .Q(t_ff_1_q[2]), .reset(_10_out));  // open: Qn, preset, en
  and _10 (_10_out, t_ff_1_q[1], t_ff_1_q[3]);
  T_Flip_Flop #(.trigger("falling")) t_ff_4 (
    .clk(t_ff_1_q[2]), .T(1'b1), .Q(t_ff_1_q[3]), .reset(_10_out));  // open: Qn, preset, en
  RAM ram_1 ();  // open: addr, data, sel, clk, ld, clr
  ROM #(.addrWidth(4), .dataWidth(7)) rom_1 (.addr(t_ff_1_q), .data(out_9));  // open: sel
  ROM #(.addrWidth(4), .dataWidth(7)) rom_2 (.addr(t_ff_1_q), .data(rom_2_data));  // open: sel
  _7_Segment_Display u_7_segment_display_2 (
    .g(out_9[3]), .f(out_9[2]), .a(out_9[1]), .b(out_9[0]), .e(out_9[6]), .d(out_9[5]), .c(out_9[4]));  // open: dp
  _7_Segment_Display u_7_segment_display_3 (
    .g(rom_2_data[3]), .f(rom_2_data[2]), .a(rom_2_data[1]), .b(rom_2_data[0]), .e(rom_2_data[6]),
    .d(rom_2_data[5]), .c(rom_2_data[4]));  // open: dp

  // Notes on the sheet:
  //   _
  //   <-
  //   _
  //   0111 0111 -> A B C D    E F G H
  //   contents of rom_1 (hex, n*v repeats v):
  //   77 11 6b 3b 1d 3e 7e 13 7f 3f
  //   contents of rom_2 (hex, n*v repeats v):
  //   3f 7f 13 7e 3e 1d 3b 6b 11 77
endmodule
