// Logisim project Temporizador.circ as structural Verilog: 12 circuits, main circuit main
module main (
);

  wire _2, _3_out, _4, _10x, _10xx, _100x, _100xx, a1, a2, a3, a4, a5, a6, a7, a8, a9, a10, a11, a12, a13,
       and_1_out, and_4_out, and_6_out, and_7_out, anos_1_out_2, anos_1_out_4, anos_2_out_2, anos_2_out_4,
       anos_3_out_2, anos_3_out_4, b1, b2, b3, b4, b5, b6, b7, b8, b9, b10, b11, b12, b13, c1, c2, c3, c4,
       c5, c6, c7, c8, c9, c10, c11, c12, c13, centena_de_dias_1_out_5, centena_de_dias_1_out_6, clock, d1,
       d2, d3, d4, d5, d6, d7, d8, d9, d10, d11, d12, d13, dezena_de_dias_1_out_3, e1, e2, e3, e4, e5, e6,
       e7, e8, e9, e10, e11, e12, e13, f1, f2, f3, f4, f5, f6, f7, f8, f9, f10, f11, f12, f13, g1, g2, g3,
       g4, g5, g6, g7, g8, g9, g10, g11, g12, g13, or_1_out, or_2_out, or_3_out, or_4_out, S1, S2, S3, S4,
       S5, S6, S7, S8, ss1, t_ff_1_q, t_ff_2_q, unidade_de_dias_1_out_3, unidade_de_horas_1_out_4,
       unidade_de_horas_1_out_6, unidade_de_meses_1_out_3, unidade_de_meses_1_out_5,
       unidade_de_semanas_1_out_3, unidade_de_semanas_1_out_5, x1, x2, xx1, xx2;

  Clock clock_1 (.out(clock));
  and and_1 (and_1_out, _4, _2);
  Dezena_de_horas dezena_de_horas_1 (
    .in_1(S1), .in_2(_4), .out_3(_2), .out_4(a2), .out_5(b2), .out_6(c2), .out_7(d2), .out_8(e2), .out_9(f2),
    .out_10(g2));
  T_Flip_Flop t_ff_1 (.clk(_10x), .T(1'b1), .Q(t_ff_1_q));  // open: Qn, preset, reset, en
  T_Flip_Flop t_ff_2 (.clk(_100x), .T(1'b1), .Q(t_ff_2_q));  // open: Qn, preset, reset, en
  nand _10 (S1, unidade_de_horas_1_out_4, unidade_de_horas_1_out_6);
  Unidade_de_horas unidade_de_horas_1 (
    .in_1(clock), .in_2(and_1_out), .out_4(unidade_de_horas_1_out_4), .out_5(_4),
    .out_6(unidade_de_horas_1_out_6), .out_3(a1), .out_8(b1), .out_9(c1), .out_10(d1), .out_11(e1),
    .out_12(f1), .out_13(g1));  // open: out_7
  Button button_1 (.out(_10x));
  Button button_2 (.out(_100x));
  and and_2 (_10xx, t_ff_1_q, clock);
  and and_3 (_100xx, t_ff_2_q, clock);
  nand _10_2 (S2, x1, unidade_de_dias_1_out_3);
  and and_4 (and_4_out, _4, _2);
  or or_1 (or_1_out, and_4_out, _10xx, _100xx);
  nand _10_3 (S3, xx1, dezena_de_dias_1_out_3);
  Unidade_de_dias unidade_de_dias_1 (
    .in_1(or_1_out), .in_2(ss1), .out_3(unidade_de_dias_1_out_3), .out_4(x2), .out_5(x1), .out_7(g3),
    .out_8(f3), .out_9(e3), .out_10(d3), .out_11(c3), .out_12(b3), .out_13(a3));  // open: out_6
  and and_5 (ss1, x1, x2, xx1, xx2, _3_out);
  and _3 (_3_out, centena_de_dias_1_out_5, centena_de_dias_1_out_6);
  _7_Segment_Display u_7_segment_display_1 (.g(g13), .f(f13), .a(a13), .b(b13), .e(e13), .d(d13), .c(c13));  // open: dp
  Dezena_de_dias dezena_de_dias_1 (
    .in_1(S2), .in_2(ss1), .out_3(dezena_de_dias_1_out_3), .out_4(xx2), .out_5(xx1), .out_7(g4), .out_8(f4),
    .out_9(e4), .out_10(d4), .out_11(c4), .out_12(b4), .out_13(a4));  // open: out_6
  Centena_de_dias centena_de_dias_1 (
    .in_1(S3), .in_2(ss1), .out_5(centena_de_dias_1_out_5), .out_6(centena_de_dias_1_out_6), .out_7(g5),
    .out_8(f5), .out_9(e5), .out_10(d5), .out_11(c5), .out_12(b5), .out_13(a5));  // open: out_3, out_4
  _7_Segment_Display u_7_segment_display_2 (.g(g12), .f(f12), .a(a12), .b(b12), .e(e12), .d(d12), .c(c12));  // open: dp
  _7_Segment_Display u_7_segment_display_3 (.g(g11), .f(f11), .a(a11), .b(b11), .e(e11), .d(d11), .c(c11));  // open: dp
  _7_Segment_Display u_7_segment_display_4 (.g(g10), .f(f10), .a(a10), .b(b10), .e(e10), .d(d10), .c(c10));  // open: dp
  nand _9 (S4, unidade_de_semanas_1_out_5, unidade_de_semanas_1_out_3);
  and and_6 (and_6_out, _4, _2);
  _7_Segment_Display u_7_segment_display_5 (.g(g8), .f(f8), .a(a8), .b(b8), .e(e8), .d(d8), .c(c8));  // open: dp
  _7_Segment_Display u_7_segment_display_6 (.g(g9), .f(f9), .a(a9), .b(b9), .e(e9), .d(d9), .c(c9));  // open: dp
  Unidade_de_semanas unidade_de_semanas_1 (
    .in_1(or_2_out), .in_2(ss1), .out_3(unidade_de_semanas_1_out_3), .out_5(unidade_de_semanas_1_out_5),
    .out_7(g6), .out_8(f6), .out_9(e6), .out_10(d6), .out_11(c6), .out_12(b6), .out_13(a6));  // open: out_4, out_6
  or or_2 (or_2_out, and_6_out, _10xx, _100xx);
  Dezena_de_semanas dezena_de_semanas_1 (
    .in_1(S4), .in_2(ss1), .out_7(g7), .out_8(f7), .out_9(e7), .out_10(d7), .out_11(c7), .out_12(b7),
    .out_13(a7));  // open: out_3, out_4, out_5, out_6
  _7_Segment_Display u_7_segment_display_7 (.g(g6), .f(f6), .a(a6), .b(b6), .e(e6), .d(d6), .c(c6));  // open: dp
  _7_Segment_Display u_7_segment_display_8 (.g(g7), .f(f7), .a(a7), .b(b7), .e(e7), .d(d7), .c(c7));  // open: dp
  nand _9_2 (S5, unidade_de_meses_1_out_5, unidade_de_meses_1_out_3);
  and and_7 (and_7_out, _4, _2);
  _7_Segment_Display u_7_segment_display_9 (.g(g4), .f(f4), .a(a4), .b(b4), .e(e4), .d(d4), .c(c4));  // open: dp
  _7_Segment_Display u_7_segment_display_10 (.g(g5), .f(f5), .a(a5), .b(b5), .e(e5), .d(d5), .c(c5));  // open: dp
  Unidade_de_meses unidade_de_meses_1 (
    .in_1(or_3_out), .in_2(ss1), .out_3(unidade_de_meses_1_out_3), .out_5(unidade_de_meses_1_out_5),
    .out_7(g8), .out_8(f8), .out_9(e8), .out_10(d8), .out_11(c8), .out_12(b8), .out_13(a8));  // open: out_4, out_6
  or or_3 (or_3_out, and_7_out, _10xx, _100xx);
  Dezena_de_meses dezena_de_meses_1 (
    .in_1(S5), .in_2(ss1), .out_7(g9), .out_8(f9), .out_9(e9), .out_10(d9), .out_11(c9), .out_12(b9),
    .out_13(a9));  // open: out_3, out_4, out_5, out_6
  _7_Segment_Display u_7_segment_display_11 (.g(g3), .f(f3), .a(a3), .b(b3), .e(e3), .d(d3), .c(c3));  // open: dp
  _7_Segment_Display u_7_segment_display_12 (.g(g1), .f(f1), .a(a1), .b(b1), .e(e1), .d(d1), .c(c1));  // open: dp
  _7_Segment_Display u_7_segment_display_13 (.g(g2), .f(f2), .a(a2), .b(b2), .e(e2), .d(d2), .c(c2));  // open: dp
  nand _9_3 (S6, anos_1_out_4, anos_1_out_2);
  Anos anos_1 (
    .in_1(or_4_out), .out_2(anos_1_out_2), .out_4(anos_1_out_4), .out_6(g10), .out_7(f10), .out_8(e10),
    .out_9(d10), .out_10(c10), .out_11(b10), .out_12(a10));  // open: out_3, out_5
  or or_4 (or_4_out, ss1, _100xx);
  nand _9_4 (S7, anos_2_out_4, anos_2_out_2);
  Anos anos_2 (
    .in_1(S6), .out_2(anos_2_out_2), .out_4(anos_2_out_4), .out_6(g11), .out_7(f11), .out_8(e11),
    .out_9(d11), .out_10(c11), .out_11(b11), .out_12(a11));  // open: out_3, out_5
  nand _9_5 (S8, anos_3_out_4, anos_3_out_2);
  Anos anos_3 (
    .in_1(S7), .out_2(anos_3_out_2), .out_4(anos_3_out_4), .out_6(g12), .out_7(f12), .out_8(e12),
    .out_9(d12), .out_10(c12), .out_11(b12), .out_12(a12));  // open: out_3, out_5
  Anos anos_4 (
    .in_1(S8), .out_6(g13), .out_7(f13), .out_8(e13), .out_9(d13), .out_10(c13), .out_11(b13), .out_12(a13));  // open: out_2, out_3, out_4, out_5

  // Notes on the sheet:
  //   ACELERAR O TEMPO
  //   ANOS
  //   MESES
  //   SEMANAS
  //   DIAS
  //   HORAS
endmodule

module Unidade_de_horas (
  input  in_1,
  input  in_2,
  output out_3,
  output out_4,
  output out_5,
  output out_6,
  output out_7,
  output out_8,
  output out_9,
  output out_10,
  output out_11,
  output out_12,
  output out_13
);

  wire _10_out, and_1_out, and_2_out, and_3_out, and_4_out, and_5_out, and_6_out, and_7_out, and_8_out,
       and_9_out, and_10_out, not_1_out, not_2_out, not_3_out, or_8_out, xnor_1_out, xnor_2_out, xor_1_out;

  not not_1 (not_1_out, out_5);
  not not_2 (not_2_out, out_6);
  not not_3 (not_3_out, out_7);
  xnor xnor_1 (xnor_1_out, out_5, out_7);
  xnor xnor_2 (xnor_2_out, out_6, out_7);
  and and_1 (and_1_out, not_1_out, not_3_out);
  and and_2 (and_2_out, not_1_out, out_6);
  and and_3 (and_3_out, out_6, not_3_out);
  and and_4 (and_4_out, out_5, not_2_out, out_7);
  and and_5 (and_5_out, not_1_out, not_3_out);
  and and_6 (and_6_out, out_6, not_3_out);
  and and_7 (and_7_out, not_2_out, not_3_out);
  and and_8 (and_8_out, out_5, not_2_out);
  and and_9 (and_9_out, out_5, not_3_out);
  xor xor_1 (xor_1_out, out_5, out_6);
  and and_10 (and_10_out, out_6, not_3_out);
  or or_1 (out_3, xnor_1_out, out_4, out_6);
  or or_2 (out_8, xnor_2_out, not_1_out);
  or or_3 (out_9, out_5, not_2_out, out_7);
  or or_4 (out_10, out_4, and_1_out, and_2_out, and_3_out, and_4_out);
  or or_5 (out_11, and_5_out, and_6_out);
  or or_6 (out_12, out_4, and_7_out, and_8_out, and_9_out);
  or or_7 (out_13, out_4, xor_1_out, and_10_out);
  T_Flip_Flop #(.trigger("falling")) t_ff_1 (
    .clk(in_1), .T(1'b1), .Q(out_7), .reset(or_8_out));  // open: Qn, preset, en
  T_Flip_Flop #(.trigger("falling")) t_ff_2 (
    .clk(out_7), .T(1'b1), .Q(out_6), .reset(or_8_out));  // open: Qn, preset, en
  or or_8 (or_8_out, in_2, _10_out);
  and _10 (_10_out, out_4, out_6);
  T_Flip_Flop #(.trigger("falling")) t_ff_3 (
    .clk(out_6), .T(1'b1), .Q(out_5), .reset(or_8_out));  // open: Qn, preset, en
  T_Flip_Flop #(.trigger("falling")) t_ff_4 (
    .clk(out_5), .T(1'b1), .Q(out_4), .reset(or_8_out));  // open: Qn, preset, en

  // Other names for the same wires on the sheet: A = out_4; B = out_5; C = out_6; D = out_7

  // Notes on the sheet:
  //   DECODIFICADOR DE 7 SEGMENTOS
endmodule

module Dezena_de_horas (
  input  in_1,
  input  in_2,
  output out_3,
  output out_4,
  output out_5,
  output out_6,
  output out_7,
  output out_8,
  output out_9,
  output out_10
);

  wire and_1_out, and_2_out, and_3_out, and_4_out, and_5_out, and_6_out, and_7_out, and_8_out, and_9_out,
       and_10_out, and_11_out, and_12_out, B, not_1_out, not_2_out, not_3_out, or_8_out, t_ff_3_q,
       xnor_1_out, xnor_2_out, xor_1_out;

  not not_1 (not_1_out, 1'b0);
  not not_2 (not_2_out, out_3);
  not not_3 (not_3_out, B);
  and and_1 (and_1_out, not_1_out, not_3_out);
  and and_2 (and_2_out, not_1_out, out_3);
  and and_3 (and_3_out, out_3, not_3_out);
  and and_4 (and_4_out, 1'b0, not_2_out, B);
  and and_5 (and_5_out, not_1_out, not_3_out);
  and and_6 (and_6_out, out_3, not_3_out);
  and and_7 (and_7_out, not_2_out, not_3_out);
  and and_8 (and_8_out, 1'b0, not_2_out);
  and and_9 (and_9_out, 1'b0, not_3_out);
  and and_10 (and_10_out, out_3, not_3_out);
  xnor xnor_1 (xnor_1_out, 1'b0, B);
  xnor xnor_2 (xnor_2_out, out_3, B);
  xor xor_1 (xor_1_out, 1'b0, out_3);
  or or_1 (out_4, xnor_1_out, 1'b0, out_3);
  or or_2 (out_5, xnor_2_out, not_1_out);
  or or_3 (out_6, 1'b0, not_2_out, B);
  or or_4 (out_7, 1'b0, and_1_out, and_2_out, and_3_out, and_4_out);
  or or_5 (out_8, and_5_out, and_6_out);
  or or_6 (out_9, 1'b0, and_7_out, and_8_out, and_9_out);
  or or_7 (out_10, 1'b0, xor_1_out, and_10_out);
  T_Flip_Flop #(.trigger("falling")) t_ff_1 (.clk(in_1), .T(1'b1), .Q(B), .reset(or_8_out));  // open: Qn, preset, en
  and and_11 (and_11_out, out_3, in_2);
  T_Flip_Flop #(.trigger("falling")) t_ff_2 (.clk(B), .T(1'b1), .Q(out_3), .reset(or_8_out));  // open: Qn, preset, en
  or or_8 (or_8_out, and_11_out, and_12_out);
  and and_12 (and_12_out, out_3, B);
  T_Flip_Flop #(.trigger("falling")) t_ff_3 (
    .clk(out_3), .T(1'b1), .Q(t_ff_3_q), .reset(or_8_out));  // open: Qn, preset, en
  T_Flip_Flop #(.trigger("falling")) t_ff_4 (.clk(t_ff_3_q), .T(1'b1), .reset(or_8_out));  // open: Q, Qn, preset, en

  // Other names for the same wires on the sheet: A = out_3

  // Notes on the sheet:
  //   DECODIFICADOR DE 7 SEGMENTOS
  //   CONTADOR DE 0 A 2
endmodule

module Unidade_de_dias (
  input  in_1,
  input  in_2,
  output out_3,
  output out_4,
  output out_5,
  output out_6,
  output out_7,
  output out_8,
  output out_9,
  output out_10,
  output out_11,
  output out_12,
  output out_13
);

  wire _10_out, or_1_out;

  Decodificador_7_Seg decodificador_7_seg_1 (
    .in_1(out_3), .in_2(out_4), .in_3(out_5), .in_4(out_6), .out_5(out_13), .out_6(out_12), .out_7(out_11),
    .out_8(out_10), .out_9(out_9), .out_10(out_8), .out_11(out_7));
  T_Flip_Flop #(.trigger("falling")) t_ff_1 (
    .clk(in_1), .T(1'b1), .Q(out_6), .reset(or_1_out));  // open: Qn, preset, en
  T_Flip_Flop #(.trigger("falling")) t_ff_2 (
    .clk(out_6), .T(1'b1), .Q(out_5), .reset(or_1_out));  // open: Qn, preset, en
  or or_1 (or_1_out, in_2, _10_out);
  and _10 (_10_out, out_3, out_5);
  T_Flip_Flop #(.trigger("falling")) t_ff_3 (
    .clk(out_5), .T(1'b1), .Q(out_4), .reset(or_1_out));  // open: Qn, preset, en
  T_Flip_Flop #(.trigger("falling")) t_ff_4 (
    .clk(out_4), .T(1'b1), .Q(out_3), .reset(or_1_out));  // open: Qn, preset, en

  // Other names for the same wires on the sheet: A = out_3; B = out_4; C = out_5; D = out_6
endmodule

module Dezena_de_dias (
  input  in_1,
  input  in_2,
  output out_3,
  output out_4,
  output out_5,
  output out_6,
  output out_7,
  output out_8,
  output out_9,
  output out_10,
  output out_11,
  output out_12,
  output out_13
);

  wire _10_out, or_1_out;

  Decodificador_7_Seg decodificador_7_seg_1 (
    .in_1(out_3), .in_2(out_4), .in_3(out_5), .in_4(out_6), .out_5(out_13), .out_6(out_12), .out_7(out_11),
    .out_8(out_10), .out_9(out_9), .out_10(out_8), .out_11(out_7));
  T_Flip_Flop #(.trigger("falling")) t_ff_1 (
    .clk(in_1), .T(1'b1), .Q(out_6), .reset(or_1_out));  // open: Qn, preset, en
  T_Flip_Flop #(.trigger("falling")) t_ff_2 (
    .clk(out_6), .T(1'b1), .Q(out_5), .reset(or_1_out));  // open: Qn, preset, en
  or or_1 (or_1_out, in_2, _10_out);
  and _10 (_10_out, out_3, out_5);
  T_Flip_Flop #(.trigger("falling")) t_ff_3 (
    .clk(out_5), .T(1'b1), .Q(out_4), .reset(or_1_out));  // open: Qn, preset, en
  T_Flip_Flop #(.trigger("falling")) t_ff_4 (
    .clk(out_4), .T(1'b1), .Q(out_3), .reset(or_1_out));  // open: Qn, preset, en

  // Other names for the same wires on the sheet: A = out_3; B = out_4; C = out_5; D = out_6
endmodule

module Centena_de_dias (
  input  in_1,
  input  in_2,
  output out_3,
  output out_4,
  output out_5,
  output out_6,
  output out_7,
  output out_8,
  output out_9,
  output out_10,
  output out_11,
  output out_12,
  output out_13
);

  wire _9_out, or_1_out;

  Decodificador_7_Seg decodificador_7_seg_1 (
    .in_1(out_3), .in_2(out_4), .in_3(out_5), .in_4(out_6), .out_5(out_13), .out_6(out_12), .out_7(out_11),
    .out_8(out_10), .out_9(out_9), .out_10(out_8), .out_11(out_7));
  T_Flip_Flop #(.trigger("falling")) t_ff_1 (
    .clk(in_1), .T(1'b1), .Q(out_6), .reset(or_1_out));  // open: Qn, preset, en
  T_Flip_Flop #(.trigger("falling")) t_ff_2 (
    .clk(out_6), .T(1'b1), .Q(out_5), .reset(or_1_out));  // open: Qn, preset, en
  or or_1 (or_1_out, in_2, _9_out);
  and _9 (_9_out, out_3, out_5);
  T_Flip_Flop #(.trigger("falling")) t_ff_3 (
    .clk(out_5), .T(1'b1), .Q(out_4), .reset(or_1_out));  // open: Qn, preset, en
  T_Flip_Flop #(.trigger("falling")) t_ff_4 (
    .clk(out_4), .T(1'b1), .Q(out_3), .reset(or_1_out));  // open: Qn, preset, en

  // Other names for the same wires on the sheet: A = out_3; B = out_4; C = out_5; D = out_6
endmodule

module Unidade_de_semanas (
  input  in_1,
  input  in_2,
  output out_3,
  output out_4,
  output out_5,
  output out_6,
  output out_7,
  output out_8,
  output out_9,
  output out_10,
  output out_11,
  output out_12,
  output out_13
);

  wire _7, _10_out, or_1_out, t_ff_1_q, t_ff_2_q, t_ff_3_q;

  Decodificador_7_Seg decodificador_7_seg_1 (
    .in_1(out_3), .in_2(out_4), .in_3(out_5), .in_4(out_6), .out_5(out_13), .out_6(out_12), .out_7(out_11),
    .out_8(out_10), .out_9(out_9), .out_10(out_8), .out_11(out_7));
  T_Flip_Flop #(.trigger("falling")) t_ff_1 (.clk(in_1), .T(1'b1), .Q(t_ff_1_q), .reset(_7));  // open: Qn, preset, en
  and and_1 (_7, t_ff_1_q, t_ff_2_q, t_ff_3_q);
  T_Flip_Flop #(.trigger("falling")) t_ff_2 (
    .clk(t_ff_1_q), .T(1'b1), .Q(t_ff_2_q), .reset(_7));  // open: Qn, preset, en
  T_Flip_Flop #(.trigger("falling")) t_ff_3 (
    .clk(t_ff_2_q), .T(1'b1), .Q(t_ff_3_q), .reset(_7));  // open: Qn, preset, en
  T_Flip_Flop #(.trigger("falling")) t_ff_4 (.clk(_7), .T(1'b1), .Q(out_6), .reset(or_1_out));  // open: Qn, preset, en
  T_Flip_Flop #(.trigger("falling")) t_ff_5 (.clk(t_ff_3_q), .T(1'b1), .reset(_7));  // open: Q, Qn, preset, en
  T_Flip_Flop #(.trigger("falling")) t_ff_6 (
    .clk(out_6), .T(1'b1), .Q(out_5), .reset(or_1_out));  // open: Qn, preset, en
  or or_1 (or_1_out, in_2, _10_out);
  and _10 (_10_out, out_3, out_5);
  T_Flip_Flop #(.trigger("falling")) t_ff_7 (
    .clk(out_5), .T(1'b1), .Q(out_4), .reset(or_1_out));  // open: Qn, preset, en
  T_Flip_Flop #(.trigger("falling")) t_ff_8 (
    .clk(out_4), .T(1'b1), .Q(out_3), .reset(or_1_out));  // open: Qn, preset, en

  // Other names for the same wires on the sheet: A = out_3; B = out_4; C = out_5; D = out_6
endmodule

module Dezena_de_semanas (
  input  in_1,
  input  in_2,
  output out_3,
  output out_4,
  output out_5,
  output out_6,
  output out_7,
  output out_8,
  output out_9,
  output out_10,
  output out_11,
  output out_12,
  output out_13
);

  Decodificador_7_Seg decodificador_7_seg_1 (
    .in_1(out_3), .in_2(out_4), .in_3(out_5), .in_4(out_6), .out_5(out_13), .out_6(out_12), .out_7(out_11),
    .out_8(out_10), .out_9(out_9), .out_10(out_8), .out_11(out_7));
  T_Flip_Flop #(.trigger("falling")) t_ff_1 (.clk(in_1), .T(1'b1), .Q(out_6), .reset(in_2));  // open: Qn, preset, en
  T_Flip_Flop #(.trigger("falling")) t_ff_2 (.clk(out_6), .T(1'b1), .Q(out_5), .reset(in_2));  // open: Qn, preset, en
  T_Flip_Flop #(.trigger("falling")) t_ff_3 (.clk(out_5), .T(1'b1), .Q(out_4), .reset(in_2));  // open: Qn, preset, en
  T_Flip_Flop #(.trigger("falling")) t_ff_4 (.clk(out_4), .T(1'b1), .Q(out_3), .reset(in_2));  // open: Qn, preset, en

  // Other names for the same wires on the sheet: A = out_3; B = out_4; C = out_5; D = out_6
endmodule

module Unidade_de_meses (
  input  in_1,
  input  in_2,
  output out_3,
  output out_4,
  output out_5,
  output out_6,
  output out_7,
  output out_8,
  output out_9,
  output out_10,
  output out_11,
  output out_12,
  output out_13
);

  wire _3, _10, _10_2_out, or_1_out, or_2_out, or_3_out, t_ff_1_q, t_ff_2_q, t_ff_3_q, t_ff_4_q, t_ff_5_q,
       t_ff_6_q, t_ff_7_q, t_ff_9_q;

  T_Flip_Flop #(.trigger("falling")) t_ff_1 (
    .clk(in_1), .T(1'b1), .Q(t_ff_1_q), .reset(or_1_out));  // open: Qn, preset, en
  and u__10 (_10, t_ff_2_q, t_ff_5_q);
  T_Flip_Flop #(.trigger("falling")) t_ff_2 (
    .clk(t_ff_1_q), .T(1'b1), .Q(t_ff_2_q), .reset(or_1_out));  // open: Qn, preset, en
  or or_1 (or_1_out, in_2, _10);
  Decodificador_7_Seg decodificador_7_seg_1 (
    .in_1(out_3), .in_2(out_4), .in_3(out_5), .in_4(out_6), .out_5(out_13), .out_6(out_12), .out_7(out_11),
    .out_8(out_10), .out_9(out_9), .out_10(out_8), .out_11(out_7));
  T_Flip_Flop #(.trigger("falling")) t_ff_3 (
    .clk(t_ff_2_q), .T(1'b1), .Q(t_ff_3_q), .reset(or_1_out));  // open: Qn, preset, en
  T_Flip_Flop #(.trigger("falling")) t_ff_4 (
    .clk(_10), .T(1'b1), .Q(t_ff_4_q), .reset(or_2_out));  // open: Qn, preset, en
  T_Flip_Flop #(.trigger("falling")) t_ff_5 (
    .clk(t_ff_3_q), .T(1'b1), .Q(t_ff_5_q), .reset(or_1_out));  // open: Qn, preset, en
  and u__3 (_3, t_ff_4_q, t_ff_6_q);
  T_Flip_Flop #(.trigger("falling")) t_ff_6 (
    .clk(t_ff_4_q), .T(1'b1), .Q(t_ff_6_q), .reset(or_2_out));  // open: Qn, preset, en
  or or_2 (or_2_out, in_2, _3);
  T_Flip_Flop #(.trigger("falling")) t_ff_7 (
    .clk(t_ff_6_q), .T(1'b1), .Q(t_ff_7_q), .reset(or_2_out));  // open: Qn, preset, en
  T_Flip_Flop #(.trigger("falling")) t_ff_8 (.clk(_3), .T(1'b1), .Q(out_6), .reset(or_3_out));  // open: Qn, preset, en
  T_Flip_Flop #(.trigger("falling")) t_ff_9 (
    .clk(t_ff_7_q), .T(1'b1), .Q(t_ff_9_q), .reset(or_2_out));  // open: Qn, preset, en
  T_Flip_Flop #(.trigger("falling")) t_ff_10 (
    .clk(out_6), .T(1'b1), .Q(out_5), .reset(or_3_out));  // open: Qn, preset, en
  or or_3 (or_3_out, in_2, _10_2_out);
  and _10_2 (_10_2_out, out_3, out_5);
  T_Flip_Flop #(.trigger("falling")) t_ff_11 (
    .clk(out_5), .T(1'b1), .Q(out_4), .reset(or_3_out));  // open: Qn, preset, en
  T_Flip_Flop #(.trigger("falling")) t_ff_12 (
    .clk(out_4), .T(1'b1), .Q(out_3), .reset(or_3_out));  // open: Qn, preset, en

  // Other names for the same wires on the sheet: A = out_3; B = out_4; C = out_5; D = out_6; x = in_2
endmodule

module Dezena_de_meses (
  input  in_1,
  input  in_2,
  output out_3,
  output out_4,
  output out_5,
  output out_6,
  output out_7,
  output out_8,
  output out_9,
  output out_10,
  output out_11,
  output out_12,
  output out_13
);

  Decodificador_7_Seg decodificador_7_seg_1 (
    .in_1(out_3), .in_2(out_4), .in_3(out_5), .in_4(out_6), .out_5(out_13), .out_6(out_12), .out_7(out_11),
    .out_8(out_10), .out_9(out_9), .out_10(out_8), .out_11(out_7));
  T_Flip_Flop #(.trigger("falling")) t_ff_1 (.clk(in_1), .T(1'b1), .Q(out_6), .reset(in_2));  // open: Qn, preset, en
  T_Flip_Flop #(.trigger("falling")) t_ff_2 (.clk(out_6), .T(1'b1), .Q(out_5), .reset(in_2));  // open: Qn, preset, en
  T_Flip_Flop #(.trigger("falling")) t_ff_3 (.clk(out_5), .T(1'b1), .Q(out_4), .reset(in_2));  // open: Qn, preset, en
  T_Flip_Flop #(.trigger("falling")) t_ff_4 (.clk(out_4), .T(1'b1), .Q(out_3), .reset(in_2));  // open: Qn, preset, en

  // Other names for the same wires on the sheet: A = out_3; B = out_4; C = out_5; D = out_6
endmodule

module Anos (
  input  in_1,
  output out_2,
  output out_3,
  output out_4,
  output out_5,
  output out_6,
  output out_7,
  output out_8,
  output out_9,
  output out_10,
  output out_11,
  output out_12
);

  wire and_1_out;

  Decodificador_7_Seg decodificador_7_seg_1 (
    .in_1(out_2), .in_2(out_3), .in_3(out_4), .in_4(out_5), .out_5(out_12), .out_6(out_11), .out_7(out_10),
    .out_8(out_9), .out_9(out_8), .out_10(out_7), .out_11(out_6));
  T_Flip_Flop #(.trigger("falling")) t_ff_1 (
    .clk(in_1), .T(1'b1), .Q(out_5), .reset(and_1_out));  // open: Qn, preset, en
  T_Flip_Flop #(.trigger("falling")) t_ff_2 (
    .clk(out_5), .T(1'b1), .Q(out_4), .reset(and_1_out));  // open: Qn, preset, en
  and and_1 (and_1_out, out_2, out_4);
  T_Flip_Flop #(.trigger("falling")) t_ff_3 (
    .clk(out_4), .T(1'b1), .Q(out_3), .reset(and_1_out));  // open: Qn, preset, en
  T_Flip_Flop #(.trigger("falling")) t_ff_4 (
    .clk(out_3), .T(1'b1), .Q(out_2), .reset(and_1_out));  // open: Qn, preset, en

  // Other names for the same wires on the sheet: A = out_2; B = out_3; C = out_4; D = out_5
endmodule

module Decodificador_7_Seg (
  input  in_1,
  input  in_2,
  input  in_3,
  input  in_4,
  output out_5,
  output out_6,
  output out_7,
  output out_8,
  output out_9,
  output out_10,
  output out_11
);

  wire and_1_out, and_2_out, and_3_out, and_4_out, and_5_out, and_6_out, and_7_out, and_8_out, and_9_out,
       and_10_out, not_1_out, not_2_out, not_3_out, xnor_1_out, xnor_2_out, xor_1_out;

  not not_1 (not_1_out, in_2);
  not not_2 (not_2_out, in_3);
  not not_3 (not_3_out, in_4);
  xnor xnor_1 (xnor_1_out, in_2, in_4);
  xnor xnor_2 (xnor_2_out, in_3, in_4);
  and and_1 (and_1_out, not_1_out, not_3_out);
  and and_2 (and_2_out, not_1_out, in_3);
  and and_3 (and_3_out, in_3, not_3_out);
  and and_4 (and_4_out, in_2, not_2_out, in_4);
  and and_5 (and_5_out, not_1_out, not_3_out);
  and and_6 (and_6_out, in_3, not_3_out);
  and and_7 (and_7_out, not_2_out, not_3_out);
  and and_8 (and_8_out, in_2, not_2_out);
  and and_9 (and_9_out, in_2, not_3_out);
  xor xor_1 (xor_1_out, in_2, in_3);
  and and_10 (and_10_out, in_3, not_3_out);
  or or_1 (out_5, xnor_1_out, in_1, in_3);
  or or_2 (out_6, xnor_2_out, not_1_out);
  or or_3 (out_7, in_2, not_2_out, in_4);
  or or_4 (out_8, in_1, and_1_out, and_2_out, and_3_out, and_4_out);
  or or_5 (out_9, and_5_out, and_6_out);
  or or_6 (out_10, in_1, and_7_out, and_8_out, and_9_out);
  or or_7 (out_11, in_1, xor_1_out, and_10_out);
endmodule
